# Fritzing sketch wiring (saved by Fritzing 0.9.3b)

parts:
  Raspberry_Pi_1 = Raspberry Pi 3 [part_number=RPI-3-V1.2]
  S4 = Round Pushbutton
  LED1 = smd LED [color="Green (565nm)" package="1206 [SMD]"]
  S5 = Round Pushbutton
  S6 = Round Pushbutton
  R5 = Resistor [tolerance=±5% resistance=220 package="2010 [SMD]"]
  LED2 = smd LED [color="Red (635nm)" package="1206 [SMD]"]
  R6 = Resistor [tolerance=±5% resistance=220 package="2010 [SMD]"]
  LED3 = smd LED [color="Yellow (592nm)" package="1206 [SMD]"]
  R7 = Resistor [tolerance=±5% resistance=220 package="2010 [SMD]"]
  R8 = Resistor [tolerance=±5% resistance=10k package=THT]
  R10 = Resistor [tolerance=±5% resistance=10k package=THT]
  R11 = Resistor [tolerance=±5% resistance=10k package=THT]

nets:
  N1: Raspberry_Pi_1.GND, S4.leg0, LED1.cathode, S5.leg0, S6.leg0, LED2.cathode, LED3.cathode
  N2: Raspberry_Pi_1.GPIO21, R8.Pin_0
  N3: Raspberry_Pi_1.GPIO20, R10.Pin_0
  N4: Raspberry_Pi_1.GPIO16, R11.Pin_0
  N5: Raspberry_Pi_1.GPIO12, R5.Pin_1
  N6: Raspberry_Pi_1.GPIO7, R6.Pin_1
  N7: Raspberry_Pi_1.GPIO8, R7.Pin_1
  N8: S4.leg1, R8.Pin_1
  N9: LED1.anode, R5.Pin_0
  N10: S5.leg1, R10.Pin_1
  N11: S6.leg1, R11.Pin_1
  N12: LED2.anode, R6.Pin_0
  N13: LED3.anode, R7.Pin_0

notes:
  Reboot Button
  Flash LED
  Reflash Button
  Flash Button
  Reflash LED
  Ready LED
